# Fritzing sketch schematics (saved by Fritzing 0.9.3b)

parts:
  Arduino_Nano_3_0 = Arduino Nano (Rev3.0)
  LDR = Photocell (LDR) [package=THT]
  DS3231RTC = ZS-042 RTC Module
  8x8_LED_Modul_mit_MAX1 = 8x8 LED Modul mit MAX7219 [package=THT]

nets:
  GND: Arduino_Nano_3_0.GND, LDR.pin_0, DS3231RTC.GND, 8x8_LED_Modul_mit_MAX1.GND_Eingang
  N1: Arduino_Nano_3_0.D11/MOSI, 8x8_LED_Modul_mit_MAX1.DIN_Eingang
  5V: Arduino_Nano_3_0.5V, DS3231RTC.VCC, 8x8_LED_Modul_mit_MAX1.VCC_Eingang
  N2: Arduino_Nano_3_0.A5, DS3231RTC.SCL
  N3: Arduino_Nano_3_0.A4, DS3231RTC.SDA
  N4: Arduino_Nano_3_0.A3, 8x8_LED_Modul_mit_MAX1.CS_Eingang
  N5: Arduino_Nano_3_0.A2, LDR.pin_1
  N6: Arduino_Nano_3_0.D13/SCK, 8x8_LED_Modul_mit_MAX1.CLK_Eingang
